# Fritzing sketch diaper_tracker_sketch (saved by Fritzing 0.9.3b)
breadboards: 1

parts:
  Raspberry_Pi_1 = Raspberry Pi 3 [part_number=RPI-3-V1.2]
  S2 = Pushbutton [package="[SMD]"]
  S3 = Pushbutton [package="[SMD]"]
  S4 = Pushbutton [package="[SMD]"]
  R1 = Resistor [tolerance=±5% resistance=220 package="0805 [SMD]"]
  R2 = Resistor [tolerance=±5% resistance=220 package="0805 [SMD]"]
  R3 = Resistor [tolerance=±5% resistance=220 package="0805 [SMD]"]

nets:
  N1: Raspberry_Pi_1.3v3, R1.Pin_1, R2.Pin_1, R3.Pin_1
  N2: Raspberry_Pi_1.GPIO23, S3.Pin_3, S3.Pin_4
  N3: Raspberry_Pi_1.GPIO15, S2.Pin_3, S2.Pin_4
  N4: Raspberry_Pi_1.GPIO14, S4.Pin_3, S4.Pin_4
  N5: S2.Pin_1, S2.Pin_2, R1.Pin_0
  N6: S3.Pin_1, S3.Pin_2, R3.Pin_0
  N7: S4.Pin_1, S4.Pin_2, R2.Pin_0
